// Logisim project proiect_var2.circ as structural Verilog
module main (
  input  reset_reg1,
  input  mode,
  input  reset_numarator,
  input  reset_reg2,
  input  in_5,
  input  in_6,
  input  in_7,
  input  in_8,
  input  in_9,
  input  in_10,
  input  in_11,
  input  in_12,
  input  reset,
  input  in_14,
  input  reset_stai,
  output [10:0] out_16
);

  wire clock_1_out, introdue_cod2_1_cod_bun, stai_15s_1_ok, switch_1_p2, switch_2_p2, switch_3_p2,
       switch_4_p1, switch_5_p2, switch_6_p2, unitate_centrala_1_acasa_led, unitate_centrala_1_cod,
       unitate_centrala_1_cod_bun_led, unitate_centrala_1_inactiv_led, unitate_centrala_1_plecat_led,
       unitate_centrala_1_sirena_led;
  wire [3:0] introdue_cod2_1_m, introdue_cod2_1_s, introdue_cod2_1_u, introdue_cod2_1_z;
  wire [6:0] hex_7seg_1_a_b_c_d_e_f_g, hex_7seg_2_a_b_c_d_e_f_g, hex_7seg_3_a_b_c_d_e_f_g,
       hex_7seg_4_a_b_c_d_e_f_g;

  Clock clock_1 (.out(clock_1_out));
  // Switch switch_1: pin names not known; wires that end beside it: 1'b1, switch_1_p2
  // Switch switch_2: pin names not known; wires that end beside it: 1'b1, switch_2_p2
  // Switch switch_3: pin names not known; wires that end beside it: 1'b1, switch_3_p2, 1'b1
  // Switch switch_4: pin names not known; wires that end beside it: switch_4_p1
  // Switch switch_5: pin names not known; wires that end beside it: 1'b1, switch_5_p2
  // Switch switch_6: pin names not known; wires that end beside it: 1'b1, switch_6_p2
  stai_15s stai_15s_1 (.clk(clock_1_out), .reset(reset_stai), .ok(stai_15s_1_ok));
  introdue_cod2 introdue_cod2_1 (
    .reset_reg1(reset_reg1), .mode(mode), .clk(clock_1_out), .reset_numarator(reset_numarator),
    .mii(switch_1_p2), .sute(switch_2_p2), .zeci(switch_3_p2), .unitati(switch_4_p1),
    .reset_reg2(reset_reg2), .m(introdue_cod2_1_m), .s(introdue_cod2_1_s), .z(introdue_cod2_1_z),
    .u(introdue_cod2_1_u), .cod_bun(introdue_cod2_1_cod_bun));
  hex_7seg hex_7seg_1 (.hex_in(introdue_cod2_1_m), .a_b_c_d_e_f_g(hex_7seg_1_a_b_c_d_e_f_g));
  hex_7seg hex_7seg_2 (.hex_in(introdue_cod2_1_s), .a_b_c_d_e_f_g(hex_7seg_2_a_b_c_d_e_f_g));
  hex_7seg hex_7seg_3 (.hex_in(introdue_cod2_1_z), .a_b_c_d_e_f_g(hex_7seg_3_a_b_c_d_e_f_g));
  hex_7seg hex_7seg_4 (.hex_in(introdue_cod2_1_u), .a_b_c_d_e_f_g(hex_7seg_4_a_b_c_d_e_f_g));
  unitate_centrala unitate_centrala_1 (
    .cod_setat(switch_5_p2), .ok(switch_6_p2), .cod_bun(introdue_cod2_1_cod_bun), .mod_acasa(in_5),
    .mod_plecat(in_6), .mod_inactiv(in_7), .geam1(in_8), .geam2(in_9), .usa(in_10), .miscare1(in_11),
    .miscare2(in_12), .stai_15s(stai_15s_1_ok), .reset(reset), .clk(clock_1_out), .activeaza(in_14),
    .cod(unitate_centrala_1_cod), .sirena_led(unitate_centrala_1_sirena_led),
    .acasa_led(unitate_centrala_1_acasa_led), .plecat_led(unitate_centrala_1_plecat_led),
    .inactiv_led(unitate_centrala_1_inactiv_led), .cod_bun_led(unitate_centrala_1_cod_bun_led), .st(out_16));
  _7_Segment_Display #(.active("false"), .decimalPoint("false")) u_7_segment_display_1 (
    .g(hex_7seg_1_a_b_c_d_e_f_g[0]), .f(hex_7seg_1_a_b_c_d_e_f_g[1]), .a(hex_7seg_1_a_b_c_d_e_f_g[6]),
    .b(hex_7seg_1_a_b_c_d_e_f_g[5]), .e(hex_7seg_1_a_b_c_d_e_f_g[2]), .d(hex_7seg_1_a_b_c_d_e_f_g[3]),
    .c(hex_7seg_1_a_b_c_d_e_f_g[4]));
  LED cod (.in(unitate_centrala_1_cod));
  LED sirena (.in(unitate_centrala_1_sirena_led));
  LED acasa_led (.in(unitate_centrala_1_acasa_led));
  LED plecat_led (.in(unitate_centrala_1_plecat_led));
  LED inactiv_led (.in(unitate_centrala_1_inactiv_led));
  LED cod_bun_led (.in(unitate_centrala_1_cod_bun_led));
  _7_Segment_Display #(.active("false"), .decimalPoint("false")) u_7_segment_display_2 (
    .g(hex_7seg_2_a_b_c_d_e_f_g[0]), .f(hex_7seg_2_a_b_c_d_e_f_g[1]), .a(hex_7seg_2_a_b_c_d_e_f_g[6]),
    .b(hex_7seg_2_a_b_c_d_e_f_g[5]), .e(hex_7seg_2_a_b_c_d_e_f_g[2]), .d(hex_7seg_2_a_b_c_d_e_f_g[3]),
    .c(hex_7seg_2_a_b_c_d_e_f_g[4]));
  _7_Segment_Display #(.active("false"), .decimalPoint("false")) u_7_segment_display_3 (
    .g(hex_7seg_3_a_b_c_d_e_f_g[0]), .f(hex_7seg_3_a_b_c_d_e_f_g[1]), .a(hex_7seg_3_a_b_c_d_e_f_g[6]),
    .b(hex_7seg_3_a_b_c_d_e_f_g[5]), .e(hex_7seg_3_a_b_c_d_e_f_g[2]), .d(hex_7seg_3_a_b_c_d_e_f_g[3]),
    .c(hex_7seg_3_a_b_c_d_e_f_g[4]));
  _7_Segment_Display #(.active("false"), .decimalPoint("false")) u_7_segment_display_4 (
    .g(hex_7seg_4_a_b_c_d_e_f_g[0]), .f(hex_7seg_4_a_b_c_d_e_f_g[1]), .a(hex_7seg_4_a_b_c_d_e_f_g[6]),
    .b(hex_7seg_4_a_b_c_d_e_f_g[5]), .e(hex_7seg_4_a_b_c_d_e_f_g[2]), .d(hex_7seg_4_a_b_c_d_e_f_g[3]),
    .c(hex_7seg_4_a_b_c_d_e_f_g[4]));
endmodule

module stai_15s (
  input  clk,
  input  reset,
  output ok
);

  wire [3:0] numarator_modulo15_1_q;

  numarator_modulo15 numarator_modulo15_1 (.clk(clk), .clear(reset), .q(numarator_modulo15_1_q));
  poarta_si_4 poarta_si_4_1 (
    .A(numarator_modulo15_1_q[0]), .B(numarator_modulo15_1_q[1]), .C(numarator_modulo15_1_q[2]),
    .D(numarator_modulo15_1_q[3]), .iesire(ok));
endmodule

module introdue_cod2 (
  input  reset_reg1,
  input  mode,
  input  clk,
  input  reset_numarator,
  input  mii,
  input  sute,
  input  zeci,
  input  unitati,
  input  reset_reg2,
  output [3:0] m,
  output [3:0] s,
  output [3:0] z,
  output [3:0] u,
  output cod_bun
);

  wire comparator_4bit_1_equal, comparator_4bit_2_equal, comparator_4bit_3_equal, comparator_4bit_4_equal;
  wire [3:0] numarator_1_q, numarator_2_q, numarator_3_q, numarator_4_q, reg_memorie_m0_1_q,
       reg_memorie_m0_2_q, reg_memorie_m0_3_q, reg_memorie_m0_4_q, registru_memorie_1_q,
       registru_memorie_2_q, registru_memorie_3_q, registru_memorie_4_q;

  numarator numarator_1 (.clk(clk), .reset(reset_numarator), .switch(mii), .q(numarator_1_q));
  numarator numarator_2 (.clk(clk), .reset(reset_numarator), .switch(sute), .q(numarator_2_q));
  numarator numarator_3 (.clk(clk), .reset(reset_numarator), .switch(zeci), .q(numarator_3_q));
  numarator numarator_4 (.clk(clk), .reset(reset_numarator), .switch(unitati), .q(numarator_4_q));
  registru_memorie registru_memorie_1 (
    .mode(mode), .reset(reset_reg1), .clk(clk), .d(numarator_1_q), .q(registru_memorie_1_q));
  registru_memorie registru_memorie_2 (
    .mode(mode), .reset(reset_reg1), .clk(clk), .d(numarator_2_q), .q(registru_memorie_2_q));
  registru_memorie registru_memorie_3 (
    .mode(mode), .reset(reset_reg1), .clk(clk), .d(numarator_3_q), .q(registru_memorie_3_q));
  registru_memorie registru_memorie_4 (
    .mode(mode), .reset(reset_reg1), .clk(clk), .d(numarator_4_q), .q(registru_memorie_4_q));
  reg_memorie_m0 reg_memorie_m0_1 (
    .mode(mode), .reset(reset_reg2), .clk(clk), .d(numarator_1_q), .q(reg_memorie_m0_1_q));
  reg_memorie_m0 reg_memorie_m0_2 (
    .mode(mode), .reset(reset_reg2), .clk(clk), .d(numarator_2_q), .q(reg_memorie_m0_2_q));
  reg_memorie_m0 reg_memorie_m0_3 (
    .mode(mode), .reset(reset_reg2), .clk(clk), .d(numarator_3_q), .q(reg_memorie_m0_3_q));
  reg_memorie_m0 reg_memorie_m0_4 (
    .mode(mode), .reset(reset_reg2), .clk(clk), .d(numarator_4_q), .q(reg_memorie_m0_4_q));
  mux2la1_4biti mux2la1_4biti_1 (.d1(registru_memorie_1_q), .d0(reg_memorie_m0_1_q), .sel(mode), .y(m));
  mux2la1_4biti mux2la1_4biti_2 (.d1(registru_memorie_2_q), .d0(reg_memorie_m0_2_q), .sel(mode), .y(s));
  mux2la1_4biti mux2la1_4biti_3 (.d1(registru_memorie_3_q), .d0(reg_memorie_m0_3_q), .sel(mode), .y(z));
  mux2la1_4biti mux2la1_4biti_4 (.d1(registru_memorie_4_q), .d0(reg_memorie_m0_4_q), .sel(mode), .y(u));
  Comparator_4bit comparator_4bit_1 (.A(registru_memorie_1_q), .B(reg_memorie_m0_1_q), .Equal(comparator_4bit_1_equal));
  Comparator_4bit comparator_4bit_2 (.A(registru_memorie_2_q), .B(reg_memorie_m0_2_q), .Equal(comparator_4bit_2_equal));
  Comparator_4bit comparator_4bit_3 (.A(registru_memorie_3_q), .B(reg_memorie_m0_3_q), .Equal(comparator_4bit_3_equal));
  Comparator_4bit comparator_4bit_4 (.A(registru_memorie_4_q), .B(reg_memorie_m0_4_q), .Equal(comparator_4bit_4_equal));
  poarta_si_4 poarta_si_4_1 (
    .A(comparator_4bit_1_equal), .B(comparator_4bit_2_equal), .C(comparator_4bit_3_equal),
    .D(comparator_4bit_4_equal), .iesire(cod_bun));
endmodule

module introduce_cod (
  input  reset_reg1,
  input  mode,
  input  clk,
  input  mii,
  input  sute,
  input  zeci,
  input  unitati,
  input  reset_reg2,
  output [3:0] m,
  output [3:0] s,
  output [3:0] z,
  output [3:0] u,
  output cod_bun
);

  wire comparator_4bit_1_equal, comparator_4bit_2_equal, comparator_4bit_3_equal, comparator_4bit_4_equal,
       undriven;
  wire [3:0] numarator_1_q, numarator_2_q, numarator_3_q, numarator_4_q, reg_memorie_m0_1_q,
       reg_memorie_m0_2_q, reg_memorie_m0_3_q, reg_memorie_m0_4_q, registru_memorie_1_q,
       registru_memorie_2_q, registru_memorie_3_q, registru_memorie_4_q;

  numarator numarator_1 (.clk(clk), .reset(undriven), .switch(mii), .q(numarator_1_q));
  numarator numarator_2 (.clk(clk), .reset(undriven), .switch(sute), .q(numarator_2_q));
  numarator numarator_3 (.clk(clk), .reset(undriven), .switch(zeci), .q(numarator_3_q));
  numarator numarator_4 (.clk(clk), .reset(undriven), .switch(unitati), .q(numarator_4_q));
  registru_memorie registru_memorie_1 (
    .mode(mode), .reset(reset_reg1), .clk(clk), .d(numarator_1_q), .q(registru_memorie_1_q));
  registru_memorie registru_memorie_2 (
    .mode(mode), .reset(reset_reg1), .clk(clk), .d(numarator_2_q), .q(registru_memorie_2_q));
  registru_memorie registru_memorie_3 (
    .mode(mode), .reset(reset_reg1), .clk(clk), .d(numarator_3_q), .q(registru_memorie_3_q));
  registru_memorie registru_memorie_4 (
    .mode(mode), .reset(reset_reg1), .clk(clk), .d(numarator_4_q), .q(registru_memorie_4_q));
  reg_memorie_m0 reg_memorie_m0_1 (
    .mode(mode), .reset(reset_reg2), .clk(clk), .d(numarator_1_q), .q(reg_memorie_m0_1_q));
  reg_memorie_m0 reg_memorie_m0_2 (
    .mode(mode), .reset(reset_reg2), .clk(clk), .d(numarator_2_q), .q(reg_memorie_m0_2_q));
  reg_memorie_m0 reg_memorie_m0_3 (
    .mode(mode), .reset(reset_reg2), .clk(clk), .d(numarator_3_q), .q(reg_memorie_m0_3_q));
  reg_memorie_m0 reg_memorie_m0_4 (
    .mode(mode), .reset(reset_reg2), .clk(clk), .d(numarator_4_q), .q(reg_memorie_m0_4_q));
  mux2la1_4biti mux2la1_4biti_1 (.d1(registru_memorie_1_q), .d0(reg_memorie_m0_1_q), .sel(mode), .y(m));
  mux2la1_4biti mux2la1_4biti_2 (.d1(registru_memorie_2_q), .d0(reg_memorie_m0_2_q), .sel(mode), .y(s));
  mux2la1_4biti mux2la1_4biti_3 (.d1(registru_memorie_3_q), .d0(reg_memorie_m0_3_q), .sel(mode), .y(z));
  mux2la1_4biti mux2la1_4biti_4 (.d1(registru_memorie_4_q), .d0(reg_memorie_m0_4_q), .sel(mode), .y(u));
  Comparator_4bit comparator_4bit_1 (.A(registru_memorie_1_q), .B(reg_memorie_m0_1_q), .Equal(comparator_4bit_1_equal));
  Comparator_4bit comparator_4bit_2 (.A(registru_memorie_2_q), .B(reg_memorie_m0_2_q), .Equal(comparator_4bit_2_equal));
  Comparator_4bit comparator_4bit_3 (.A(registru_memorie_3_q), .B(reg_memorie_m0_3_q), .Equal(comparator_4bit_3_equal));
  Comparator_4bit comparator_4bit_4 (.A(registru_memorie_4_q), .B(reg_memorie_m0_4_q), .Equal(comparator_4bit_4_equal));
  poarta_si_4 poarta_si_4_1 (
    .A(comparator_4bit_1_equal), .B(comparator_4bit_2_equal), .C(comparator_4bit_3_equal),
    .D(comparator_4bit_4_equal), .iesire(cod_bun));
endmodule

// VHDL entity numarator_modulo15, as the project stores it:
LIBRARY ieee;
USE ieee.std_logic_1164.all;
USE ieee.numeric_std.all;

ENTITY numarator_modulo15 IS

  PORT ( q: out std_logic_vector(3 downto 0);
  	   clk: in std_logic;
  	   clear: in std_logic);
  	   
END numarator_modulo15;
	
ARCHITECTURE TypeArchitecture OF numarator_modulo15 IS

	signal intermediar: integer;

BEGIN
	process(clk, clear)
		begin
			if clear='1' then intermediar<=0;
				elsif rising_edge(clk) then intermediar<=intermediar+1;
					if intermediar=15 then intermediar<=0;
					end if;
			end if;
				q<=std_logic_vector(to_unsigned(intermediar, q'length));
	end process;
	
END TypeArchitecture;

// VHDL entity registru_memorie, as the project stores it:
LIBRARY ieee;
USE ieee.std_logic_1164.all;
USE ieee.numeric_std.all;

ENTITY registru_memorie IS

  PORT (mode: in std_logic;
	   reset: in std_logic;
  	   clk: in std_logic;
  	   d: in std_logic_vector(3 downto 0);
  	   q: out std_logic_vector(3 downto 0));
  	   
END registru_memorie;

ARCHITECTURE TypeArchitecture OF registru_memorie IS
	signal temporar:std_logic_vector(3 downto 0):="0000";
BEGIN
	process(clk, reset)
		begin 
			if reset='1' then temporar<= (others => '0');
				elsif rising_edge(clk) then 
					if mode='1' then temporar<=d;
					end if;
			end if;
	q<=temporar;
	end process;


END TypeArchitecture;

// VHDL entity hex_7seg, as the project stores it:
LIBRARY ieee;
USE ieee.std_logic_1164.all;

ENTITY hex_7seg IS

  PORT ( hex_in: in std_logic_vector(3 downto 0);
  		a_b_c_d_e_f_g: out std_logic_vector(6 downto 0));

END hex_7seg;

ARCHITECTURE TypeArchitecture OF hex_7seg IS

BEGIN
	a_b_c_d_e_f_g <= "0000001" when hex_in= x"0" else
				  "1001111" when hex_in= x"1" else
				  "0010010" when hex_in= x"2" else
				  "0000110" when hex_in= x"3" else
				  "1001100" when hex_in= x"4" else
				  "0100100" when hex_in= x"5" else
				  "0100000" when hex_in= x"6" else
				  "0001111" when hex_in= x"7" else
				  "0000000" when hex_in= x"8" else
				  "0000100" when hex_in= x"9" else
				  "0001000" when hex_in= x"A" else
				  "1100000" when hex_in= x"B" else
				  "0110001" when hex_in= x"C" else
				  "1000010" when hex_in= x"d" else
				  "0110000" when hex_in= x"E" else
				  "0111000" when hex_in= x"F" else
				  "1111111";

END TypeArchitecture;

// VHDL entity numarator, as the project stores it:
LIBRARY ieee;
USE ieee.std_logic_1164.all;
USE ieee.numeric_std.all;

ENTITY numarator IS

  PORT (q: out std_logic_vector(3 downto 0);
  	   clk: in std_logic;
  	   reset: in std_logic;
  	   switch: in std_logic);
  	   
END numarator;
	
ARCHITECTURE TypeArchitecture OF numarator IS


	signal intermediar: integer:=0;

BEGIN
	process(clk, reset)
		begin
			if reset='1' then intermediar<=0;
				elsif rising_edge(clk) then 
					if switch='1' then intermediar<=intermediar+1;
					end if;
			end if;
				q<=std_logic_vector(to_unsigned(intermediar, q'length));
	end process;
	
END TypeArchitecture;

// VHDL entity unitate_centrala, as the project stores it:
LIBRARY ieee;
USE ieee.std_logic_1164.all;

ENTITY unitate_centrala IS

  PORT (cod_setat, ok, cod_bun, mod_acasa, mod_plecat, mod_inactiv, geam1, geam2, usa, miscare1, miscare2, stai_15s, reset ,clk, activeaza: in std_logic;
  	   cod, sirena_led, acasa_led, plecat_led, inactiv_led, cod_bun_led : out std_logic;
  	   st: out std_logic_vector(10 downto 0)
  	   );

END unitate_centrala;

ARCHITECTURE TypeArchitecture OF unitate_centrala IS

	type stare_t is(admin, waiting, verificare_cod, aleg_mod, acasa_activ, plecat_activ, stare_inactiv, plecat, sirena_activa);

	signal stare, next_stare: stare_t;
	
BEGIN

	actualizare_stare: process(clk)
		begin
			if clk='1' and rising_edge(clk)  then stare <= next_stare;
			end if;
		end process actualizare_stare;
	stari: process(cod_setat, ok, cod_bun, mod_acasa, mod_plecat, mod_inactiv, geam1, geam2, usa, miscare1, miscare2, stai_15s, reset ,clk, activeaza)
				begin
	
		case stare is
				when admin => if cod_setat='1' then  next_stare<=waiting;
								else next_stare<=admin;
							end if;
				when waiting =>if ok='1' then next_stare<=verificare_cod;
								else next_stare<=waiting;
							end if;
				when verificare_cod=>if cod_bun='1' then next_stare<=aleg_mod;
									else next_stare<=waiting;
								end if;
				when aleg_mod=>if mod_acasa='1' then next_stare<=acasa_activ; --clear la numarator?
								elsif mod_plecat='1' then next_stare<=plecat;
									elsif mod_inactiv='1' then next_stare<=stare_inactiv;
										else next_stare<=aleg_mod;
							end if;
				when acasa_activ=>if geam1='1' or usa='1' or geam2='1' then next_stare<=sirena_activa;
									else next_stare<=acasa_activ;  
							  end if;
				when sirena_activa=> if reset='0' then next_stare<=sirena_activa;
									else next_stare<=waiting;
								end if;
				when plecat=>if stai_15s='1' then  next_stare<=plecat_activ; --enable pt numarator?
								else next_stare<=plecat;
						   end if;
				when plecat_activ=>if geam1='1' or geam2='1' or usa='1' or miscare1='1' or miscare2='1' then next_stare<=sirena_activa;
									else next_stare<=plecat_activ;
							    end if;
				when stare_inactiv=> if activeaza='1' then next_stare<=waiting;
									else next_stare<=stare_inactiv;
							   	  end if;
			end case;
		end process stari;
leduri: process(stare, cod_setat, cod_bun)
		begin
			cod<='0'; sirena_led<='0'; acasa_led<='0'; plecat_led<='0'; inactiv_led<='0'; cod_bun_led<='0'; 
				case stare is
					when admin => if cod_setat='1' then cod<='1';
								end if;
								st(10)<='1';
					when waiting => cod<='0';
								st(9) <= '1';
					when verificare_cod=> if cod_bun='1' then cod_bun_led<='1';
										end if;
								st(8) <= '1';
					when aleg_mod =>cod_bun_led<='0';
								st(7) <= '1';
					when acasa_activ => acasa_led<='1';
								st(6) <= '1';
					when plecat_activ => plecat_led<='1';
								st(5) <= '1';
					when stare_inactiv =>inactiv_led<='1';
								st(4) <= '1';
					when sirena_activa => sirena_led<='1'; 
								st(3) <= '1';
					when others=> acasa_led<='0';
				end case;
		end process leduri;
END TypeArchitecture;

// VHDL entity Comparator_4bit, as the project stores it:
library ieee;
use ieee.std_logic_1164.all;

entity Comparator_4bit is
    port (
        A, B: in std_logic_vector(3 downto 0);
        Equal: out std_logic
    );
end entity Comparator_4bit;

architecture Behavioral of Comparator_4bit is
begin
    process(A, B)
    begin
        if A = B then
            Equal <= '1';
        else
        		Equal <= '0';
        end if;
    end process;
end architecture Behavioral;

// VHDL entity poarta_si_4, as the project stores it:
library ieee;
use ieee.std_logic_1164.all;

entity poarta_si_4 is
    port (
        A, B, C, D: in std_logic;
        iesire: out std_logic
    );
end entity poarta_si_4;

architecture Behavioral of poarta_si_4 is
begin
    process(A, B, C, D)
    begin
        iesire <= A and B and C and D;
    end process;
end architecture Behavioral;

// VHDL entity reg_memorie_m0, as the project stores it:
LIBRARY ieee;
USE ieee.std_logic_1164.all;

USE ieee.numeric_std.all;

ENTITY reg_memorie_m0 IS

  PORT (
mode: in std_logic;
	   reset: in std_logic;
  	   clk: in std_logic;
  	   d: in std_logic_vector(3 downto 0);
  	   q: out std_logic_vector(3 downto 0));
  	   
END reg_memorie_m0 ;

ARCHITECTURE TypeArchitecture OF reg_memorie_m0  IS

	signal temporar1:std_logic_vector(3 downto 0):="0000";
BEGIN
	process(clk, reset)
		begin 
			if reset='1' then temporar1<= (others => '0');

				elsif rising_edge(clk) then 
					if mode='0' then temporar1<=d;
					end if;
			end if;
	q<=temporar1;
	end process;


END TypeArchitecture;

// VHDL entity mux2la1_4biti, as the project stores it:
LIBRARY ieee;
USE ieee.std_logic_1164.all;

ENTITY mux2la1_4biti IS
  PORT (d1, d0: in std_logic_vector(3 downto 0); 
  	    sel: in std_logic;
  	    y: out std_logic_vector(3 downto 0));	
END mux2la1_4biti;

 
ARCHITECTURE mux_4biti OF mux2la1_4biti IS
BEGIN
	process(sel, d0, d1)
  		begin
    			if sel = '0' then
      			y <= d0;  
    			else
      			y <= d1;   
    			end if;
    	end process;
END mux_4biti;
